// Logisim project computer.circ as structural Verilog
module semiadder (
  input  A,
  input  B,
  output U,
  output S
);

  and and_1 (U, A, B);
  xor xor_1 (S, A, B);
endmodule

module fulladder (
  input  A,
  input  B,
  input  D,
  output U,
  output S
);

  wire semiadder_1_s, semiadder_1_u, semiadder_2_u;

  semiadder semiadder_1 (.A(A), .B(B), .U(semiadder_1_u), .S(semiadder_1_s));
  semiadder semiadder_2 (.A(semiadder_1_s), .B(D), .U(semiadder_2_u), .S(S));
  or or_1 (U, semiadder_1_u, semiadder_2_u);
endmodule

module Add_8 (
  input  A0,
  input  A1,
  input  A2,
  input  A3,
  input  A4,
  input  A5,
  input  A6,
  input  AN,
  input  B0,
  input  B1,
  input  B2,
  input  B3,
  input  B4,
  input  B5,
  input  B6,
  input  BN,
  output S0,
  output S1,
  output S2,
  output S3,
  output S4,
  output S5,
  output S6,
  output SN,
  output SO
);

  wire fulladder_1_u, fulladder_2_u, fulladder_3_u, fulladder_4_u, fulladder_5_u, fulladder_6_u,
       semiadder_1_u;

  semiadder semiadder_1 (.A(A0), .B(B0), .U(semiadder_1_u), .S(S0));
  fulladder fulladder_1 (.A(A1), .B(B1), .D(semiadder_1_u), .U(fulladder_1_u), .S(S1));
  fulladder fulladder_2 (.A(A2), .B(B2), .D(fulladder_1_u), .U(fulladder_2_u), .S(S2));
  fulladder fulladder_3 (.A(A3), .B(B3), .D(fulladder_2_u), .U(fulladder_3_u), .S(S3));
  fulladder fulladder_4 (.A(A4), .B(B4), .D(fulladder_3_u), .U(fulladder_4_u), .S(S4));
  fulladder fulladder_5 (.A(A5), .B(B5), .D(fulladder_4_u), .U(fulladder_5_u), .S(S5));
  fulladder fulladder_6 (.A(A6), .B(B6), .D(fulladder_5_u), .U(fulladder_6_u), .S(S6));
  fulladder fulladder_7 (.A(AN), .B(BN), .D(fulladder_6_u), .U(SO), .S(SN));
endmodule

module Sel_2 (
  input  L_0_5295f36e,
  input  L_1_e4c21882,
  input  S,
  output U
);

  wire and_1_out, and_2_out, not_1_out;

  and and_1 (and_1_out, L_0_5295f36e, not_1_out);
  not not_1 (not_1_out, S);
  and and_2 (and_2_out, L_1_e4c21882, S);
  or or_1 (U, and_1_out, and_2_out);
endmodule

module Sel_8 (
  input  A0,
  input  A1,
  input  A2,
  input  A3,
  input  A4,
  input  A5,
  input  A6,
  input  AN,
  input  B0,
  input  B1,
  input  B2,
  input  B3,
  input  B4,
  input  B5,
  input  S,
  input  B6,
  input  BN,
  output S0,
  output S1,
  output S2,
  output S3,
  output S4,
  output S5,
  output S6,
  output SN
);

  Sel_2 sel_2_1 (.L_0_5295f36e(A0), .L_1_e4c21882(B0), .S(S), .U(S0));
  Sel_2 sel_2_2 (.L_0_5295f36e(A1), .L_1_e4c21882(B1), .S(S), .U(S1));
  Sel_2 sel_2_3 (.L_0_5295f36e(A2), .L_1_e4c21882(B2), .S(S), .U(S2));
  Sel_2 sel_2_4 (.L_0_5295f36e(A3), .L_1_e4c21882(B3), .S(S), .U(S3));
  Sel_2 sel_2_5 (.L_0_5295f36e(A4), .L_1_e4c21882(B4), .S(S), .U(S4));
  Sel_2 sel_2_6 (.L_0_5295f36e(A5), .L_1_e4c21882(B5), .S(S), .U(S5));
  Sel_2 sel_2_7 (.L_0_5295f36e(A6), .L_1_e4c21882(B6), .S(S), .U(S6));
  Sel_2 sel_2_8 (.L_0_5295f36e(AN), .L_1_e4c21882(BN), .S(S), .U(SN));
endmodule

module Sel_8_M (
  input  [7:0] A,
  input  [7:0] B,
  input  in_3,
  output [7:0] S
);

  Sel_2 sel_2_1 (.L_0_5295f36e(A[0]), .L_1_e4c21882(B[0]), .S(in_3), .U(S[0]));
  Sel_2 sel_2_2 (.L_0_5295f36e(A[1]), .L_1_e4c21882(B[1]), .S(in_3), .U(S[1]));
  Sel_2 sel_2_3 (.L_0_5295f36e(A[2]), .L_1_e4c21882(B[2]), .S(in_3), .U(S[2]));
  Sel_2 sel_2_4 (.L_0_5295f36e(A[3]), .L_1_e4c21882(B[3]), .S(in_3), .U(S[3]));
  Sel_2 sel_2_5 (.L_0_5295f36e(A[4]), .L_1_e4c21882(B[4]), .S(in_3), .U(S[4]));
  Sel_2 sel_2_6 (.L_0_5295f36e(A[5]), .L_1_e4c21882(B[5]), .S(in_3), .U(S[5]));
  Sel_2 sel_2_7 (.L_0_5295f36e(A[6]), .L_1_e4c21882(B[6]), .S(in_3), .U(S[6]));
  Sel_2 sel_2_8 (.L_0_5295f36e(A[7]), .L_1_e4c21882(B[7]), .S(in_3), .U(S[7]));
endmodule

module SW_8 (
  input  A0,
  input  A1,
  input  A2,
  input  A3,
  input  A4,
  input  A5,
  input  S,
  input  A6,
  input  AN,
  output S0,
  output S1,
  output S2,
  output S3,
  output S4,
  output S5,
  output S6,
  output SN
);

  Sel_8 sel_8_1 (
    .A0(1'b0), .A1(1'b0), .A2(1'b0), .A3(1'b0), .A4(1'b0), .A5(1'b0), .A6(1'b0), .AN(1'b0), .B0(A0), .B1(A1),
    .B2(A2), .B3(A3), .B4(A4), .B5(A5), .B6(A6), .BN(AN), .S(S), .S0(S0), .S1(S1), .S2(S2), .S3(S3), .S4(S4),
    .S5(S5), .S6(S6), .SN(SN));
endmodule

module SW_8_M (
  input  [7:0] B,
  input  in_2,
  output [7:0] S
);

  Sel_8 sel_8_1 (
    .A0(1'b0), .A1(1'b0), .A2(1'b0), .A3(1'b0), .A4(1'b0), .A5(1'b0), .A6(1'b0), .AN(1'b0), .B0(B[0]),
    .B1(B[1]), .B2(B[2]), .B3(B[3]), .B4(B[4]), .B5(B[5]), .B6(B[6]), .BN(B[7]), .S(in_2), .S0(S[0]),
    .S1(S[1]), .S2(S[2]), .S3(S[3]), .S4(S[4]), .S5(S[5]), .S6(S[6]), .SN(S[7]));
endmodule

module Div_2 (
  input  S,
  input  L_0_5295f36e,
  output U0,
  output U1
);

  wire not_1_out;

  not not_1 (not_1_out, S);
  and and_1 (U0, not_1_out, L_0_5295f36e);
  and and_2 (U1, L_0_5295f36e, S);
endmodule

module Div_8_M (
  input  [7:0] D,
  input  in_2,
  output [7:0] A,
  output [7:0] B
);

  Div_2 div_2_1 (.L_0_5295f36e(D[0]), .S(in_2), .U0(A[0]), .U1(B[0]));
  Div_2 div_2_2 (.L_0_5295f36e(D[1]), .S(in_2), .U0(A[1]), .U1(B[1]));
  Div_2 div_2_3 (.L_0_5295f36e(D[2]), .S(in_2), .U0(A[2]), .U1(B[2]));
  Div_2 div_2_4 (.L_0_5295f36e(D[3]), .S(in_2), .U0(A[3]), .U1(B[3]));
  Div_2 div_2_5 (.L_0_5295f36e(D[4]), .S(in_2), .U0(A[4]), .U1(B[4]));
  Div_2 div_2_6 (.L_0_5295f36e(D[5]), .S(in_2), .U0(A[5]), .U1(B[5]));
  Div_2 div_2_7 (.L_0_5295f36e(D[6]), .S(in_2), .U0(A[6]), .U1(B[6]));
  Div_2 div_2_8 (.L_0_5295f36e(D[7]), .S(in_2), .U0(A[7]), .U1(B[7]));
endmodule

module D_Ratch (
  input  S,
  input  D,
  input  CLK,
  input  E,
  input  R,
  output U,
  output NOT_U_ac6da121
);

  wire and_1_out, and_2_out, and_3_out, and_4_out, nor_1_out, nor_2_out, nor_3_out;

  and and_1 (and_1_out, D, CLK);
  and and_2 (and_2_out, CLK, E);
  nor nor_1 (nor_1_out, S, R);
  and and_3 (and_3_out, and_1_out, and_2_out, nor_1_out);
  and and_4 (and_4_out, nor_1_out, ~and_1_out, and_2_out);  // AND_Gate
  nor nor_2 (nor_2_out, S, and_3_out);
  nor nor_3 (nor_3_out, and_4_out, R);
  nand nand_1 (U, nor_2_out, NOT_U_ac6da121);
  nand nand_2 (NOT_U_ac6da121, U, nor_3_out);
endmodule

module D_8 (
  input  [7:0] D,
  input  CLK,
  input  E,
  input  R,
  output [7:0] U
);

  D_Ratch d_ratch_1 (.D(D[0]), .CLK(CLK), .E(E), .S(1'b0), .R(R), .U(U[0]));  // open: NOT_U_ac6da121
  D_Ratch d_ratch_2 (.D(D[1]), .CLK(CLK), .E(E), .S(1'b0), .R(R), .U(U[1]));  // open: NOT_U_ac6da121
  D_Ratch d_ratch_3 (.D(D[2]), .CLK(CLK), .E(E), .S(1'b0), .R(R), .U(U[2]));  // open: NOT_U_ac6da121
  D_Ratch d_ratch_4 (.D(D[3]), .CLK(CLK), .E(E), .S(1'b0), .R(R), .U(U[3]));  // open: NOT_U_ac6da121
  D_Ratch d_ratch_5 (.D(D[4]), .CLK(CLK), .E(E), .S(1'b0), .R(R), .U(U[4]));  // open: NOT_U_ac6da121
  D_Ratch d_ratch_6 (.D(D[5]), .CLK(CLK), .E(E), .S(1'b0), .R(R), .U(U[5]));  // open: NOT_U_ac6da121
  D_Ratch d_ratch_7 (.D(D[6]), .CLK(CLK), .E(E), .S(1'b0), .R(R), .U(U[6]));  // open: NOT_U_ac6da121
  D_Ratch d_ratch_8 (.D(D[7]), .CLK(CLK), .E(E), .S(1'b0), .R(R), .U(U[7]));  // open: NOT_U_ac6da121
endmodule

module M_S_D_Flip_Flop (
  input  D,
  input  CLK,
  input  E,
  input  R,
  output U
);

  wire d_ratch_1_u, not_1_out;

  D_Ratch d_ratch_1 (.D(D), .CLK(CLK), .E(E), .S(1'b0), .R(R), .U(d_ratch_1_u));  // open: NOT_U_ac6da121
  not not_1 (not_1_out, CLK);
  D_Ratch d_ratch_2 (.D(d_ratch_1_u), .CLK(not_1_out), .E(E), .S(1'b0), .R(R), .U(U));  // open: NOT_U_ac6da121
endmodule

module M_S_D_8 (
  input  [7:0] D,
  input  CLK,
  input  E,
  input  R,
  output [7:0] U
);

  wire not_1_out;
  wire [7:0] d_8_1_u;

  D_8 d_8_1 (.D(D), .CLK(CLK), .E(E), .R(R), .U(d_8_1_u));
  not not_1 (not_1_out, CLK);
  D_8 d_8_2 (.D(d_8_1_u), .CLK(not_1_out), .E(E), .R(R), .U(U));
endmodule

module Merger_8 (
  input  A0,
  input  A1,
  input  A2,
  input  A3,
  input  A4,
  input  A5,
  input  A6,
  input  AN,
  input  B0,
  input  B1,
  input  B2,
  input  B3,
  input  B4,
  input  B5,
  input  B6,
  input  BN,
  output S0,
  output S1,
  output S2,
  output S3,
  output S4,
  output S5,
  output S6,
  output SN
);

  or or_1 (S0, A0, B0);
  or or_2 (S1, A1, B1);
  or or_3 (S2, A2, B2);
  or or_4 (S3, A3, B3);
  or or_5 (S4, A4, B4);
  or or_6 (S5, A5, B5);
  or or_7 (S6, A6, B6);
  or or_8 (SN, AN, BN);
endmodule

module Counter_2 (
  input  E,
  input  CLK,
  input  C,
  output L_0,
  output L_1
);

  J_K_Flip_Flop #(.trigger("falling")) j_k_ff_1 (.J(E), .K(E), .clk(CLK), .Q(L_0), .reset(C));  // open: Qn, preset
  J_K_Flip_Flop #(.trigger("falling")) j_k_ff_2 (.J(E), .K(E), .clk(L_0), .Q(L_1), .reset(C));  // open: Qn, preset
endmodule

module Counter_8 (
  input  E,
  input  CLK,
  input  C,
  output L_0,
  output L_1,
  output L_2,
  output L_3,
  output L_4,
  output L_5,
  output L_6,
  output L_7
);

  J_K_Flip_Flop #(.trigger("falling")) j_k_ff_1 (.J(E), .K(E), .clk(CLK), .Q(L_0), .reset(C));  // open: Qn, preset
  J_K_Flip_Flop #(.trigger("falling")) j_k_ff_2 (.J(E), .K(E), .clk(L_0), .Q(L_1), .reset(C));  // open: Qn, preset
  J_K_Flip_Flop #(.trigger("falling")) j_k_ff_3 (.J(E), .K(E), .clk(L_1), .Q(L_2), .reset(C));  // open: Qn, preset
  J_K_Flip_Flop #(.trigger("falling")) j_k_ff_4 (.J(E), .K(E), .clk(L_2), .Q(L_3), .reset(C));  // open: Qn, preset
  J_K_Flip_Flop #(.trigger("falling")) j_k_ff_5 (.J(E), .K(E), .clk(L_3), .Q(L_4), .reset(C));  // open: Qn, preset
  J_K_Flip_Flop #(.trigger("falling")) j_k_ff_6 (.J(E), .K(E), .clk(L_4), .Q(L_5), .reset(C));  // open: Qn, preset
  J_K_Flip_Flop #(.trigger("falling")) j_k_ff_7 (.J(E), .K(E), .clk(L_5), .Q(L_6), .reset(C));  // open: Qn, preset
  J_K_Flip_Flop #(.trigger("falling")) j_k_ff_8 (.J(E), .K(E), .clk(L_6), .Q(L_7), .reset(C));  // open: Qn, preset
endmodule

module Inverter (
  input  A0,
  input  A1,
  input  A2,
  input  A3,
  input  A4,
  input  A5,
  input  A6,
  input  AN,
  output S0,
  output S1,
  output S2,
  output S3,
  output S4,
  output S5,
  output S6,
  output SN,
  output SO
);

  wire not_1_out, not_2_out, not_3_out, not_4_out, not_5_out, not_6_out, not_7_out;

  not not_1 (not_1_out, A0);
  not not_2 (not_2_out, A1);
  not not_3 (not_3_out, A2);
  not not_4 (not_4_out, A3);
  not not_5 (not_5_out, A4);
  not not_6 (not_6_out, A5);
  not not_7 (not_7_out, A6);
  not not_8 (SN, AN);
  Add_8 add_8_1 (
    .A0(not_1_out), .A1(not_2_out), .A2(not_3_out), .A3(not_4_out), .A4(not_5_out), .A5(not_6_out),
    .A6(not_7_out), .AN(1'b0), .B0(1'b1), .B1(1'b0), .B2(1'b0), .B3(1'b0), .B4(1'b0), .B5(1'b0), .B6(1'b0),
    .BN(1'b0), .S0(S0), .S1(S1), .S2(S2), .S3(S3), .S4(S4), .S5(S5), .S6(S6), .SO(SO));  // open: SN
endmodule

module AddSub (
  input  A0,
  input  A1,
  input  A2,
  input  A3,
  input  A4,
  input  A5,
  input  A6,
  input  AN,
  input  RUN,
  input  CLK,
  input  SUB,
  input  B0,
  input  B1,
  input  B2,
  input  B3,
  input  B4,
  input  B5,
  input  B6,
  input  BN,
  output S0,
  output S1,
  output S2,
  output S3,
  output S4,
  output S5,
  output S6,
  output SN
);

  wire and_1_out, and_2_out, inverter_1_s0, inverter_1_s1, inverter_1_s2, inverter_1_s3, inverter_1_s4,
       inverter_1_s5, inverter_1_s6, inverter_1_sn, sel_8_1_s0, sel_8_1_s1, sel_8_1_s2, sel_8_1_s3,
       sel_8_1_s4, sel_8_1_s5, sel_8_1_s6, sel_8_1_sn, sw_8_1_s0, sw_8_1_s1, sw_8_1_s2, sw_8_1_s3, sw_8_1_s4,
       sw_8_1_s5, sw_8_1_s6, sw_8_1_sn, sw_8_2_s0, sw_8_2_s1, sw_8_2_s2, sw_8_2_s3, sw_8_2_s4, sw_8_2_s5,
       sw_8_2_s6, sw_8_2_sn;

  and and_1 (and_1_out, RUN, CLK);
  and and_2 (and_2_out, and_1_out, SUB);
  SW_8 sw_8_1 (
    .A0(B0), .A1(B1), .A2(B2), .A3(B3), .A4(B4), .A5(B5), .A6(B6), .AN(BN), .S(and_1_out), .S0(sw_8_1_s0),
    .S1(sw_8_1_s1), .S2(sw_8_1_s2), .S3(sw_8_1_s3), .S4(sw_8_1_s4), .S5(sw_8_1_s5), .S6(sw_8_1_s6),
    .SN(sw_8_1_sn));
  SW_8 sw_8_2 (
    .A0(AN), .A1(A6), .A2(A5), .A3(A4), .A4(A3), .A5(A2), .A6(A1), .AN(A0), .S(and_1_out), .S0(sw_8_2_s0),
    .S1(sw_8_2_s1), .S2(sw_8_2_s2), .S3(sw_8_2_s3), .S4(sw_8_2_s4), .S5(sw_8_2_s5), .S6(sw_8_2_s6),
    .SN(sw_8_2_sn));
  Inverter inverter_1 (
    .A0(sw_8_1_s0), .A1(sw_8_1_s1), .A2(sw_8_1_s2), .A3(sw_8_1_s3), .A4(sw_8_1_s4), .A5(sw_8_1_s5),
    .A6(sw_8_1_s6), .AN(sw_8_1_sn), .S0(inverter_1_s0), .S1(inverter_1_s1), .S2(inverter_1_s2),
    .S3(inverter_1_s3), .S4(inverter_1_s4), .S5(inverter_1_s5), .S6(inverter_1_s6), .SN(inverter_1_sn));  // open: SO
  Sel_8 sel_8_1 (
    .A0(sw_8_1_s0), .A1(sw_8_1_s1), .A2(sw_8_1_s2), .A3(sw_8_1_s3), .A4(sw_8_1_s4), .A5(sw_8_1_s5),
    .A6(sw_8_1_s6), .AN(sw_8_1_sn), .B0(inverter_1_s0), .B1(inverter_1_s1), .B2(inverter_1_s2),
    .B3(inverter_1_s3), .B4(inverter_1_s4), .B5(inverter_1_s5), .B6(inverter_1_s6), .BN(inverter_1_sn),
    .S(and_2_out), .S0(sel_8_1_s0), .S1(sel_8_1_s1), .S2(sel_8_1_s2), .S3(sel_8_1_s3), .S4(sel_8_1_s4),
    .S5(sel_8_1_s5), .S6(sel_8_1_s6), .SN(sel_8_1_sn));
  Add_8 add_8_1 (
    .A0(sw_8_2_sn), .A1(sw_8_2_s6), .A2(sw_8_2_s5), .A3(sw_8_2_s4), .A4(sw_8_2_s3), .A5(sw_8_2_s2),
    .A6(sw_8_2_s1), .AN(sw_8_2_s0), .B0(sel_8_1_s0), .B1(sel_8_1_s1), .B2(sel_8_1_s2), .B3(sel_8_1_s3),
    .B4(sel_8_1_s4), .B5(sel_8_1_s5), .B6(sel_8_1_s6), .BN(sel_8_1_sn), .S0(S0), .S1(S1), .S2(S2), .S3(S3),
    .S4(S4), .S5(S5), .S6(S6), .SN(SN));  // open: SO
endmodule

module Buffer (
  input  [7:0] in_1,
  input  [7:0] in_2,
  input  [7:0] D2,
  input  R,
  input  CLK,
  input  W,
  output [3:0] P,
  output [3:0] C,
  output [7:0] D1,
  output [7:0] out_10
);

  wire not_1_out;
  wire [7:0] C2_u, C3_u, C4_u, C5_u, CT2_u, CT3_u, CT4_u, CT5_u, D1CT4_u, D1T2_u, D1T3_u, D1T5_u, D2T2_u,
       D2T3_u, D2T4_u, D2T5_u, D12_u, D13_u, D14_u, D15_u, D22_u, D23_u, D24_u, D25_u;

  D_8 C5 (.D(in_1), .CLK(CLK), .E(W), .R(R), .U(C5_u));
  D_8 CT5 (.D(C5_u), .CLK(not_1_out), .E(W), .R(R), .U(CT5_u));
  D_8 D15 (.D(in_2), .CLK(CLK), .E(W), .R(R), .U(D15_u));
  D_8 D1T5 (.D(D15_u), .CLK(not_1_out), .E(W), .R(R), .U(D1T5_u));
  D_8 D25 (.D(D2), .CLK(CLK), .E(W), .R(R), .U(D25_u));
  D_8 D2T5 (.D(D25_u), .CLK(not_1_out), .E(W), .R(R), .U(D2T5_u));
  not not_1 (not_1_out, CLK);
  D_8 C4 (.D(CT5_u), .CLK(CLK), .E(W), .R(R), .U(C4_u));
  D_8 CT4 (.D(C4_u), .CLK(not_1_out), .E(W), .R(R), .U(CT4_u));
  D_8 D14 (.D(D1T5_u), .CLK(CLK), .E(W), .R(R), .U(D14_u));
  D_8 D1CT4 (.D(D14_u), .CLK(not_1_out), .E(W), .R(R), .U(D1CT4_u));
  D_8 D24 (.D(D2T5_u), .CLK(CLK), .E(W), .R(R), .U(D24_u));
  D_8 D2T4 (.D(D24_u), .CLK(not_1_out), .E(W), .R(R), .U(D2T4_u));
  D_8 C3 (.D(CT4_u), .CLK(CLK), .E(W), .R(R), .U(C3_u));
  D_8 D13 (.D(D1CT4_u), .CLK(CLK), .E(W), .R(R), .U(D13_u));
  D_8 D23 (.D(D2T4_u), .CLK(CLK), .E(W), .R(R), .U(D23_u));
  D_8 CT3 (.D(C3_u), .CLK(not_1_out), .E(W), .R(R), .U(CT3_u));
  D_8 C2 (.D(CT3_u), .CLK(CLK), .E(W), .R(R), .U(C2_u));
  D_8 D1T3 (.D(D13_u), .CLK(not_1_out), .E(W), .R(R), .U(D1T3_u));
  D_8 D12 (.D(D1T3_u), .CLK(CLK), .E(W), .R(R), .U(D12_u));
  D_8 D2T3 (.D(D23_u), .CLK(not_1_out), .E(W), .R(R), .U(D2T3_u));
  D_8 D22 (.D(D2T3_u), .CLK(CLK), .E(W), .R(R), .U(D22_u));
  D_8 CT2 (.D(C2_u), .CLK(not_1_out), .E(W), .R(R), .U(CT2_u));
  D_8 D1T2 (.D(D12_u), .CLK(not_1_out), .E(W), .R(R), .U(D1T2_u));
  D_8 D2T2 (.D(D22_u), .CLK(not_1_out), .E(W), .R(R), .U(D2T2_u));
  D_8 C1 (.D(CT2_u), .CLK(CLK), .E(W), .R(R), .U({C, P}));
  D_8 D11 (.D(D1T2_u), .CLK(CLK), .E(W), .R(R), .U(D1));
  D_8 D21 (.D(D2T2_u), .CLK(CLK), .E(W), .R(R), .U(out_10));
endmodule

module PU (
  input  [7:0] D1,
  input  R,
  input  CLK,
  input  E,
  input  [3:0] C,
  input  [7:0] D2,
  output [7:0] O
);

  wire and_1_out, and_2_out, and_3_out, and_4_out, clock_1_out, m_s_d_flip_flop_1_u, nand_1_out, nand_2_out,
       nor_1_out, not_1_out, not_2_out, not_3_out, or_1_out, or_2_out, sel_2_1_u;
  wire [7:0] addsub_1_s0, counter_8_1_l_0, d_8_1_u, m_s_d_8_1_u, m_s_d_8_2_u, sel_8_m_1_s, sel_8_m_2_s,
       sel_8_m_3_s, sel_8_m_4_s, sw_8_m_1_s, xor_1_out;

  Clock clock_1 (.out(clock_1_out));
  and and_1 (and_1_out, clock_1_out, E);
  Sel_8_M sel_8_m_1 (.A(addsub_1_s0), .B(D1), .in_3(and_3_out), .S(sel_8_m_1_s));
  M_S_D_8 m_s_d_8_1 (.CLK(and_1_out), .E(C[1]), .R(or_1_out), .D(sel_8_m_1_s), .U(m_s_d_8_1_u));
  Sel_8_M sel_8_m_2 (.A(D1), .B(m_s_d_8_1_u), .in_3(C[1]), .S(sel_8_m_2_s));
  Sel_8_M sel_8_m_3 (.A(D2), .B(sel_8_m_4_s), .in_3(C[1]), .S(sel_8_m_3_s));
  Sel_8_M sel_8_m_4 (.A(m_s_d_8_2_u), .B(d_8_1_u), .in_3(C[0]), .S(sel_8_m_4_s));
  D_8 d_8_1 (.D(D2), .CLK(and_1_out), .E(and_3_out), .R(or_1_out), .U(d_8_1_u));
  AddSub addsub_1 (
    .RUN(E), .CLK(clock_1_out), .SUB(C[0]), .A0(sel_8_m_2_s[0]), .A1(sel_8_m_2_s[1]), .A2(sel_8_m_2_s[2]),
    .A3(sel_8_m_2_s[3]), .A4(sel_8_m_2_s[4]), .A5(sel_8_m_2_s[5]), .A6(sel_8_m_2_s[6]), .AN(sel_8_m_2_s[7]),
    .B0(sel_8_m_3_s[0]), .B1(sel_8_m_3_s[1]), .B2(sel_8_m_3_s[2]), .B3(sel_8_m_3_s[3]), .B4(sel_8_m_3_s[4]),
    .B5(sel_8_m_3_s[5]), .B6(sel_8_m_3_s[6]), .BN(sel_8_m_3_s[7]), .S0(addsub_1_s0[0]), .S1(addsub_1_s0[1]),
    .S2(addsub_1_s0[2]), .S3(addsub_1_s0[3]), .S4(addsub_1_s0[4]), .S5(addsub_1_s0[5]), .S6(addsub_1_s0[6]),
    .SN(addsub_1_s0[7]));
  M_S_D_8 m_s_d_8_2 (.CLK(and_1_out), .E(C[1]), .R(or_1_out), .D(D1), .U(m_s_d_8_2_u));
  or or_1 (or_1_out, and_2_out, R);
  assign xor_1_out = d_8_1_u ^ counter_8_1_l_0;  // XOR_Gate xor_1, 8 bits wide
  and and_2 (and_2_out, and_1_out, m_s_d_flip_flop_1_u);
  not not_1 (not_1_out, addsub_1_s0[7]);
  and and_3 (and_3_out, C[1], nor_1_out);
  not not_2 (not_2_out, or_2_out);
  or or_2 (or_2_out, xor_1_out[0], xor_1_out[1], xor_1_out[2], xor_1_out[3], xor_1_out[4], xor_1_out[5], xor_1_out[6], xor_1_out[7]);
  Sel_2 sel_2_1 (.L_0_5295f36e(or_2_out), .L_1_e4c21882(not_1_out), .S(C[0]), .U(sel_2_1_u));
  nor nor_1 (nor_1_out, counter_8_1_l_0[7], counter_8_1_l_0[6], counter_8_1_l_0[5], counter_8_1_l_0[4], counter_8_1_l_0[3], counter_8_1_l_0[2], counter_8_1_l_0[1], counter_8_1_l_0[0]);
  Counter_8 counter_8_1 (
    .E(sel_2_1_u), .CLK(and_1_out), .C(or_1_out), .L_0(counter_8_1_l_0[0]), .L_1(counter_8_1_l_0[1]),
    .L_2(counter_8_1_l_0[2]), .L_3(counter_8_1_l_0[3]), .L_4(counter_8_1_l_0[4]), .L_5(counter_8_1_l_0[5]),
    .L_6(counter_8_1_l_0[6]), .L_7(counter_8_1_l_0[7]));
  nand nand_1 (nand_1_out, nand_2_out, C[1]);
  nand nand_2 (nand_2_out, not_2_out, not_3_out);
  not not_3 (not_3_out, sel_2_1_u);
  SW_8_M sw_8_m_1 (.B(addsub_1_s0), .in_2(nand_1_out), .S(sw_8_m_1_s));
  and and_4 (and_4_out, not_3_out, C[1], C[0]);
  M_S_D_Flip_Flop m_s_d_flip_flop_1 (
    .D(nand_1_out), .CLK(and_1_out), .E(and_1_out), .R(or_1_out), .U(m_s_d_flip_flop_1_u));
  Sel_8_M sel_8_m_5 (.A(sw_8_m_1_s), .B(counter_8_1_l_0), .in_3(and_4_out), .S(O));

  // Notes on the sheet:
  //   CLK
  //   1
  //   1
  //   CLK
  //   CLK
  //   1
  //   1
  //   0
  //   CLK
endmodule

module CPU (
  input  C0,
  input  C1,
  input  C2,
  input  C3,
  input  C4,
  input  C5,
  input  C6,
  input  C7,
  input  D10,
  input  D11,
  input  D12,
  input  D13,
  input  D14,
  input  D15,
  input  D16,
  input  D17,
  input  D20,
  input  D21,
  input  D22,
  input  D23,
  input  D24,
  input  D25,
  input  D26,
  input  D27
);
endmodule
