// Logisim project flipflop.circ as structural Verilog
module SR_NOR (
  input  S,
  input  R,
  output Q,
  output nQ
);

  nor nor_1 (nQ, S, Q);
  nor nor_2 (Q, nQ, R);
endmodule

module SR_NAND (
  input  nS,
  input  nR,
  output Q,
  output nQ
);

  nand nand_1 (Q, nS, nQ);
  nand nand_2 (nQ, Q, nR);
endmodule

module SR_AND_OR (
  input  S,
  input  R,
  output Q
);

  wire not_1_out, or_1_out;

  or or_1 (or_1_out, S, Q);
  not not_1 (not_1_out, R);
  and and_1 (Q, or_1_out, not_1_out);
endmodule

module Gated_SR_NAND (
  input  S,
  input  E,
  input  R,
  output Q,
  output nQ
);

  wire nand_1_out, nand_2_out;

  nand nand_1 (nand_1_out, S, E);
  nand nand_2 (nand_2_out, E, R);
  nand nand_3 (Q, nand_1_out, nQ);
  nand nand_4 (nQ, Q, nand_2_out);
endmodule

module Gated_D_NAND (
  input  D,
  input  E,
  output Q,
  output nQ
);

  wire nand_1_out, nand_2_out;

  nand nand_1 (nand_1_out, D, E);
  nand nand_2 (nand_2_out, nand_1_out, E);
  nand nand_3 (Q, nand_1_out, nQ);
  nand nand_4 (nQ, Q, nand_2_out);

  // Notes on the sheet:
  //   =not D if E=1
endmodule

module D_Flip_Flop (
  input  S,
  input  D,
  input  E,
  input  R,
  output out_5,
  output out_6
);

  wire and_1_out, and_2_out, and_3_out, and_4_out, nor_1_out, nor_2_out, nor_3_out;

  and and_1 (and_1_out, D, E);
  and and_2 (and_2_out, ~D, E);  // AND_Gate
  nor nor_1 (nor_1_out, S, R);
  and and_3 (and_3_out, and_1_out, nor_1_out);
  and and_4 (and_4_out, nor_1_out, and_2_out);
  nor nor_2 (nor_2_out, S, and_3_out);
  nor nor_3 (nor_3_out, and_4_out, R);
  nand nand_1 (out_5, nor_2_out, out_6);
  nand nand_2 (out_6, out_5, nor_3_out);
endmodule
